// Digital circuit CPU.dig as structural Verilog
module CPU (
  input  clk,
  input  reset,
  input  \int ,
  input  ibus_done,
  input  [47:0] ibus_idata,
  input  dbus_done,
  input  [47:0] dbus_idata,
  output [14:0] ibus_addr,
  output ibus_fetch,
  output dbus_read,
  output dbus_write,
  output [14:0] dbus_addr,
  output [47:0] dbus_odata
);

  wire acc_is_zero, alu_done, and_1_out, C_active, C_sel_mem, C_write, decode, isOpCached, M_i_is_zero, m_w,
       P_R_ADD, P_SEL_ADDR, w_acc, w_opcode, w_pc;
  wire [0:0] PC;
  wire [1:0] P_SEL_MR, P_SEL_MW;
  wire [2:0] P_SEL_ACC, P_SEL_MD, P_SEL_PC;
  wire [3:0] multiplexer_1_out, multiplexer_2_out, op_ir, reg_index;
  wire [5:0] R_q;
  wire [8:0] P_IMM;
  wire [14:0] add_1_s, add_3_s, C_q, M_i, M_r, multiplexer_4_out, multiplexer_5_out, multiplexer_10_out,
       multiplexer_11_out, op_addr, pcCached_q, sub_1_s, U_addr, V_addr;
  wire [15:0] add_2_s, multiplexer_7_out, multiplexer_8_out, multiplexer_9_out;
  wire [23:0] opCache_q, opCache_q_2, opcode;
  wire [47:0] alu_result, multiplexer_3_out, Y;

  Register #(.Bits(6)) R (.D(6'b000001), .C(clk), .en(1'b0), .Q(R_q));
  // ALU alu_1: pin names not known; wires that end beside it: alu_result, alu_done
  Add #(.Bits(15)) add_1 (.a(M_r), .b(15'h1), .c_i(1'b0), .s(add_1_s));  // open: c_o
  Sub #(.Bits(15)) sub_1 (.a(M_r), .b(15'h1), .c_i(1'b0), .s(sub_1_s));  // open: c_o
  Multiplexer #(.Selector_Bits(2), .Bits(4)) multiplexer_1 (
    .sel(P_SEL_MW), .in_0(reg_index), .in_1(P_IMM[3:0]), .in_2(V_addr[3:0]), .in_3(U_addr[3:0]),
    .out(multiplexer_1_out));
  Multiplexer #(.Selector_Bits(2), .Bits(4)) multiplexer_2 (
    .sel(P_SEL_MR), .in_0(reg_index), .in_1(P_IMM[3:0]), .in_2(V_addr[3:0]), .in_3(U_addr[3:0]),
    .out(multiplexer_2_out));
  Multiplexer #(.Selector_Bits(3), .Bits(48)) multiplexer_3 (
    .sel(P_SEL_ACC), .in_0(dbus_idata), .in_1({{33{1'b0}}, M_r}), .in_2({{42{1'b0}}, R_q}), .in_3(Y),
    .in_4(alu_result), .in_5(alu_result), .in_6(alu_result), .in_7(alu_result), .out(multiplexer_3_out));
  Multiplexer #(.Selector_Bits(3), .Bits(15)) multiplexer_4 (
    .sel(P_SEL_MD), .in_0(ibus_addr), .in_1(dbus_odata[14:0]), .in_2(M_r), .in_3(add_1_s), .in_4(sub_1_s),
    .in_5(V_addr), .in_6(U_addr), .in_7(U_addr), .out(multiplexer_4_out));
  RegisterFile #(.AddrBits(4), .Bits(15)) M_regs (
    .Din(multiplexer_4_out), .we(m_w), .Rw(multiplexer_1_out), .C(clk), .Ra(reg_index),
    .Rb(multiplexer_2_out), .Da(M_i), .Db(M_r));
  Register #(.Bits(48)) ACC (.D(multiplexer_3_out), .C(clk), .en(w_acc), .Q(dbus_odata));
  Register #(.Bits(48)) u_Y (.D(48'h1), .C(clk), .en(1'b0), .Q(Y));
  Comparator #(.Bits(15)) comparator_1 (.a({15{1'b0}}), .b(M_i), .eq(M_i_is_zero));  // open: gt, lt
  Comparator #(.Bits(48)) comparator_2 (.a({48{1'b0}}), .b(dbus_odata), .eq(acc_is_zero));  // open: gt, lt
  Add #(.Bits(16)) add_2 (.a({ibus_addr, PC[0]}), .b(16'h1), .c_i(1'b0), .s(add_2_s));  // open: c_o
  Multiplexer #(.Bits(15)) multiplexer_5 (
    .sel(C_sel_mem), .in_0(U_addr), .in_1(dbus_idata[14:0]), .out(multiplexer_5_out));
  ControlUnit controlunit_1 (
    .clk(clk), .reset(reset), .irq(\int ), .ibus_done(ibus_done), .dbus_done(dbus_done), .alu_done(alu_done),
    .isOpCached(isOpCached), .acc_iszero(acc_is_zero), .acc_isneg(dbus_odata[40]), .Mi_iszero(M_i_is_zero),
    .opcode(opcode), .decode(decode), .C_wr(C_write), .C_src(C_sel_mem), .C_active(C_active),
    .op_addr(op_addr), .op_ir(op_ir), .P_R_ADD(P_R_ADD), .m_w(m_w), .P_SEL_MW(P_SEL_MW), .P_IMM(P_IMM),
    .w_opcode(w_opcode), .w_pc(w_pc), .P_SEL_PC(P_SEL_PC), .w_acc(w_acc), .P_SEL_ACC(P_SEL_ACC),
    .P_SEL_MR(P_SEL_MR), .P_SEL_MD(P_SEL_MD), .ibus_fetch(ibus_fetch), .dbus_read(dbus_read),
    .dbus_write(dbus_write), .P_SEL_ADDR(P_SEL_ADDR));
  and and_1 (and_1_out, decode, isOpCached);
  Multiplexer #(.Bits(15)) multiplexer_6 (.sel(P_SEL_ADDR), .in_0(U_addr), .in_1(M_r), .out(dbus_addr));
  Multiplexer #(.Selector_Bits(3), .Bits(16)) multiplexer_7 (
    .sel(P_SEL_PC), .in_0({U_addr, 1'b0}), .in_1({V_addr, 1'b0}), .in_2({M_i, 1'b0}),
    .in_3({{6{1'b0}}, P_IMM, 1'b0}), .in_4(add_2_s), .in_5({U_addr, 1'b0}), .in_6({U_addr, 1'b0}),
    .in_7({U_addr, 1'b0}), .out(multiplexer_7_out));
  Multiplexer #(.Bits(16)) multiplexer_8 (
    .sel(and_1_out), .in_0({ibus_addr, PC[0]}), .in_1(add_2_s), .out(multiplexer_8_out));
  Register #(.Bits(15)) C (.D(multiplexer_5_out), .C(clk), .en(C_write), .Q(C_q));
  Multiplexer #(.Bits(16)) multiplexer_9 (
    .sel(w_pc), .in_0(multiplexer_8_out), .in_1(multiplexer_7_out), .out(multiplexer_9_out));
  Add #(.Bits(15)) add_3 (.a(op_addr), .b(C_q), .c_i(1'b0), .s(add_3_s));  // open: c_o
  Multiplexer #(.Bits(15)) multiplexer_10 (.sel(C_active), .in_0(op_addr), .in_1(add_3_s), .out(multiplexer_10_out));
  Multiplexer #(.Bits(15)) multiplexer_11 (.sel(P_R_ADD), .in_0(V_addr), .in_1(M_r), .out(multiplexer_11_out));
  Register #(.Bits(16)) u_PC (.D(multiplexer_9_out), .C(clk), .en(1'b1), .Q({ibus_addr, PC[0]}));
  Register #(.Bits(48)) opCache (.D(ibus_idata), .C(clk), .en(w_opcode), .Q({opCache_q_2, opCache_q}));
  Register #(.Bits(15)) pcCached (.D(ibus_addr), .C(clk), .en(w_opcode), .Q(pcCached_q));
  Multiplexer #(.Bits(24)) multiplexer_12 (.sel(PC[0]), .in_0(opCache_q_2), .in_1(opCache_q), .out(opcode));
  Comparator #(.Bits(15)) comparator_3 (.a(pcCached_q), .b(ibus_addr), .eq(isOpCached));  // open: gt, lt
  Register #(.Bits(15)) u_V_addr (.D(multiplexer_10_out), .C(clk), .en(decode), .Q(V_addr));
  Register #(.Bits(4)) u_reg_index (.D(op_ir), .C(clk), .en(decode), .Q(reg_index));
  Add #(.Bits(15)) add_4 (.a(multiplexer_11_out), .b(M_i), .c_i(1'b0), .s(U_addr));  // open: c_o

  // Other names for the same wires on the sheet: ACC[47:0] = dbus_odata; acc_is_neg = dbus_odata[40];
  //   interrupt = \int ; PC[15:1] = ibus_addr
endmodule
