// Digital circuit ControlUnit.dig as structural Verilog
module ControlUnit (
  input  clk,
  input  reset,
  input  irq,
  input  ibus_done,
  input  dbus_done,
  input  alu_done,
  input  isOpCached,
  input  acc_iszero,
  input  acc_isneg,
  input  Mi_iszero,
  input  [23:0] opcode,
  output decode,
  output C_wr,
  output C_src,
  output C_active,
  output [14:0] op_addr,
  output [3:0] op_ir,
  output P_R_ADD,
  output m_w,
  output [1:0] P_SEL_MW,
  output [8:0] P_IMM,
  output w_opcode,
  output w_pc,
  output [2:0] P_SEL_PC,
  output w_acc,
  output [2:0] P_SEL_ACC,
  output [1:0] P_SEL_MR,
  output [2:0] P_SEL_MD,
  output ibus_fetch,
  output dbus_read,
  output dbus_write,
  output P_SEL_ADDR
);

  wire and_1_out, and_2_out, and_3_out, and_6_out, and_7_out, and_12_out, and_13_out, and_14_out, and_15_out,
       and_16_out, and_17_out, and_18_out, branch, busy, comparator_1_eq, gie, irq_t, multiplexer_1_out,
       multiplexer_2_out, not_1_out, not_2_out, not_3_out, not_4_out, not_5_out, not_6_out, not_7_out,
       not_8_out, not_9_out, not_10_out, not_11_out, not_12_out, not_13_out, not_14_out, op_lflag, or_1_out,
       or_2_out, or_3_out, or_5_out, P_A_NEG, P_A_NONZERO, P_A_ZERO, P_BRANCH, P_DECODE, P_ENTER_INT,
       P_EXIT_INT, P_M_NONZERO, P_M_W, P_M_ZERO, P_OP_NOT_CACHED, P_SEL_ALU_MEM, P_W_A, P_W_C, P_W_OPCODE,
       P_W_PC;
  wire [3:0] op_lcmd;
  wire [5:0] op_scmd, P_ALU;

  and and_1 (and_1_out, irq, gie);
  not not_1 (not_1_out, busy);
  and and_2 (and_2_out, P_ENTER_INT, not_1_out);
  and and_3 (and_3_out, not_1_out, P_EXIT_INT);
  not not_2 (not_2_out, busy);
  Multiplexer multiplexer_1 (.sel(reset), .in_0(and_1_out), .in_1(1'b0), .out(multiplexer_1_out));
  or or_1 (or_1_out, reset, and_2_out);
  and and_4 (C_wr, not_2_out, P_W_C);
  opSplitter opsplitter_1 (
    .opcode(opcode), .op_ir(op_ir), .op_lflag(op_lflag), .op_scmd(op_scmd), .op_lcmd(op_lcmd),
    .op_addr(op_addr));
  uSeq useq_1 (
    .clk(clk), .reset(reset), .busy(busy), .branch(branch), .decode(decode), .irq(irq_t), .opcode(opcode),
    .uop({P_SEL_ALU_MEM, P_M_ZERO, P_W_PC, P_EXIT_INT, P_ENTER_INT, C_active, P_BRANCH, P_A_ZERO, P_A_NEG, P_A_NONZERO, P_W_C, P_W_A, dbus_write, dbus_read, P_DECODE, P_W_OPCODE, ibus_fetch, P_OP_NOT_CACHED, C_src, P_R_ADD, P_SEL_ADDR, P_SEL_PC, P_M_NONZERO, P_SEL_MR, P_M_W, P_SEL_MW, P_SEL_MD, P_SEL_ACC, P_ALU, P_IMM}));
  Register u_irq (.D(multiplexer_1_out), .C(clk), .en(1'b1), .Q(irq_t));
  or or_2 (or_2_out, and_3_out, reset, and_2_out);
  Multiplexer multiplexer_2 (.sel(or_1_out), .in_0(and_3_out), .in_1(1'b0), .out(multiplexer_2_out));
  Register u_gie (.D(multiplexer_2_out), .C(clk), .en(or_2_out), .Q(gie));
  not not_3 (not_3_out, busy);
  or or_3 (or_3_out, dbus_read, dbus_write);
  not not_4 (not_4_out, dbus_done);
  not not_5 (not_5_out, ibus_done);
  Comparator #(.Bits(6)) comparator_1 (.a(P_ALU), .b({6{1'b0}}), .eq(comparator_1_eq));  // open: gt, lt
  not not_6 (not_6_out, alu_done);
  not not_7 (not_7_out, busy);
  not not_8 (not_8_out, busy);
  not not_9 (not_9_out, busy);
  not not_10 (not_10_out, busy);
  and and_5 (decode, not_3_out, P_DECODE);
  and and_6 (and_6_out, or_3_out, not_4_out);
  and and_7 (and_7_out, ibus_fetch, not_5_out);
  not not_11 (not_11_out, comparator_1_eq);
  not not_12 (not_12_out, isOpCached);
  not not_13 (not_13_out, acc_iszero);
  not not_14 (not_14_out, Mi_iszero);
  and and_8 (m_w, not_7_out, P_M_W);
  and and_9 (w_opcode, not_8_out, P_W_OPCODE);
  and and_10 (w_pc, not_9_out, P_W_PC);
  and and_11 (w_acc, not_10_out, P_W_A);
  and and_12 (and_12_out, not_11_out, not_6_out);
  and and_13 (and_13_out, not_12_out, P_OP_NOT_CACHED);
  and and_14 (and_14_out, acc_iszero, P_A_ZERO);
  and and_15 (and_15_out, not_13_out, P_A_NONZERO);
  and and_16 (and_16_out, Mi_iszero, P_M_ZERO);
  and and_17 (and_17_out, not_14_out, P_M_NONZERO);
  and and_18 (and_18_out, acc_isneg, P_A_NEG);
  or or_4 (busy, and_6_out, and_7_out, and_12_out);
  or or_5 (or_5_out, and_13_out, and_14_out, and_15_out, and_16_out, and_17_out);
  or or_6 (branch, or_5_out, and_18_out, P_BRANCH);

  // Other names for the same wires on the sheet: P_SEL_C_MEM = C_src; P_FETCH = ibus_fetch; P_MEM_R = dbus_read;
  //   P_MEM_W = dbus_write; P_C_ACTIVE = C_active; interrupt = irq
endmodule
