// Digital circuit DRAM.dig as structural Verilog
module DRAM (
  input  clk,
  input  read,
  input  write,
  input  [14:0] addr,
  input  [47:0] idata,
  output done,
  output [47:0] odata
);

  wire comparator_1_eq, or_1_out;
  wire [47:0] DRAM_d, multiplexer_1_out;

  or or_1 (or_1_out, read, write);
  RAMDualPort #(.AddrBits(15), .Bits(48)) DRAM (.A(addr), .Din(idata), .str(write), .C(clk), .ld(read), .D(DRAM_d));
  Comparator #(.Bits(15)) comparator_1 (.a(addr), .b({15{1'b0}}), .eq(comparator_1_eq));  // open: gt, lt
  Multiplexer multiplexer_1 (.sel(comparator_1_eq), .in_0(DRAM_d[0]), .in_1(1'b0), .out(multiplexer_1_out[0]));
  Register register_1 (.D(or_1_out), .C(clk), .en(1'b1), .Q(done));
  Register #(.Bits(48)) register_2 (.D(multiplexer_1_out), .C(clk), .en(read), .Q(odata));
  // Pins of 1 and 48 bits meet at DRAM_d
  // Pins of 1 and 48 bits meet at multiplexer_1_out
  // Pins of 1 and 48 bits meet at {48{1'b0}}
endmodule
