// Digital circuit IROM.dig as structural Verilog
module IROM (
  input  clk,
  input  read,
  input  [14:0] addr,
  output done,
  output [47:0] data
);

  wire and_1_out, not_1_out;
  wire [47:0] IROM_d;

  Register u_done (.D(read), .C(clk), .en(1'b1), .Q(done));
  ROM #(.AddrBits(15), .Bits(48)) IROM (.A(addr), .sel(1'b1), .D(IROM_d));
  not not_1 (not_1_out, done);
  and and_1 (and_1_out, read, not_1_out);
  Register #(.Bits(48)) register_1 (.D(IROM_d), .C(clk), .en(and_1_out), .Q(data));

  // Notes on the sheet:
  //   addr: Instruction ROM
endmodule
