// Digital circuit MESM6.dig as structural Verilog
module MESM6 (
  input  clk
);

  wire cpu_1_dbus_read, cpu_1_dbus_write, cpu_1_ibus_fetch, dram_1_done, irom_1_done, reset_1_out;
  wire [14:0] cpu_1_dbus_addr, cpu_1_ibus_addr;
  wire [47:0] cpu_1_dbus_odata, dram_1_odata, irom_1_data;

  Reset #(.invertOutput("false")) reset_1 (.out(reset_1_out));
  IROM irom_1 (.clk(clk), .read(cpu_1_ibus_fetch), .addr(cpu_1_ibus_addr), .done(irom_1_done), .data(irom_1_data));
  CPU cpu_1 (
    .clk(clk), .reset(reset_1_out), .\int (1'b0), .ibus_done(irom_1_done), .ibus_idata(irom_1_data),
    .dbus_done(dram_1_done), .dbus_idata(dram_1_odata), .ibus_addr(cpu_1_ibus_addr),
    .ibus_fetch(cpu_1_ibus_fetch), .dbus_read(cpu_1_dbus_read), .dbus_write(cpu_1_dbus_write),
    .dbus_addr(cpu_1_dbus_addr), .dbus_odata(cpu_1_dbus_odata));
  DRAM dram_1 (
    .clk(clk), .read(cpu_1_dbus_read), .write(cpu_1_dbus_write), .addr(cpu_1_dbus_addr),
    .idata(cpu_1_dbus_odata), .done(dram_1_done), .odata(dram_1_odata));
endmodule
