// Digital circuit aluAddCarry.dig as structural Verilog
module aluAddCarry (
  input  [47:0] A,
  input  [47:0] B,
  input  [3:0] count,
  input  [47:0] R,
  input  [47:0] Y,
  output [47:0] R_next,
  output [47:0] Y_next,
  output done
);

  wire add_1_c_o;
  wire [47:0] add_1_s, add_2_s, multiplexer_2_out;

  Add #(.Bits(48)) add_1 (.a(A), .b(B), .c_i(1'b0), .s(add_1_s), .c_o(add_1_c_o));
  Add #(.Bits(48)) add_2 (.a(48'h1), .b(R), .c_i(1'b0), .s(add_2_s));  // open: c_o
  Multiplexer #(.Bits(48)) multiplexer_1 (.sel(count[0]), .in_0(add_1_s), .in_1(multiplexer_2_out), .out(R_next));
  Multiplexer #(.Bits(48)) multiplexer_2 (.sel(add_1_c_o), .in_0(add_1_s), .in_1(add_2_s), .out(multiplexer_2_out));
  Multiplexer #(.Bits(48)) multiplexer_3 (.sel(count[0]), .in_0({48{1'b0}}), .in_1(Y), .out(Y_next));

  assign done = count[0];
endmodule
