// Digital circuit opSplitter.dig as structural Verilog
module opSplitter (
  input  [23:0] opcode,
  output [3:0] op_ir,
  output op_lflag,
  output [5:0] op_scmd,
  output [3:0] op_lcmd,
  output [14:0] op_addr
);

  Multiplexer #(.Bits(15)) multiplexer_1 (
    .sel(opcode[19]), .in_0({{3{opcode[18]}}, opcode[11:0]}), .in_1(opcode[14:0]), .out(op_addr));

  assign op_ir = opcode[23:20];
  assign op_lcmd = opcode[18:15];
  assign op_lflag = opcode[19];
  assign op_scmd = opcode[17:12];
endmodule
