// Digital circuit uSeq.dig as structural Verilog
module uSeq (
  input  clk,
  input  reset,
  input  busy,
  input  branch,
  input  decode,
  input  irq,
  input  [23:0] opcode,
  output [50:0] uop
);

  wire and_1_out, comparator_1_eq, comparator_2_eq, comparator_3_eq, not_1_out, op_lflag, or_1_out;
  wire [3:0] op_ir, op_lcmd;
  wire [5:0] op_scmd;
  wire [8:0] add_1_s, entry16_d, entry64_d, multiplexer_1_out, multiplexer_2_out, multiplexer_3_out,
       multiplexer_4_out, multiplexer_5_out, multiplexer_6_out, multiplexer_7_out, uPC_q;
  wire [50:0] multiplexer_8_out, uROM_d;

  ROM #(.AddrBits(6), .Bits(9)) entry64 (.A(op_scmd), .sel(1'b1), .D(entry64_d));
  ROM #(.AddrBits(4), .Bits(9)) entry16 (.A(op_lcmd), .sel(1'b1), .D(entry16_d));
  Comparator #(.Bits(24)) comparator_1 (.a(opcode), .b(24'h90000), .eq(comparator_1_eq));  // open: gt, lt
  Comparator #(.Bits(24)) comparator_2 (.a(opcode), .b(24'h8000), .eq(comparator_2_eq));  // open: gt, lt
  Comparator #(.Bits(24)) comparator_3 (.a(opcode), .b(24'h22000), .eq(comparator_3_eq));  // open: gt, lt
  opSplitter opsplitter_1 (
    .opcode(opcode), .op_ir(op_ir), .op_lflag(op_lflag), .op_scmd(op_scmd), .op_lcmd(op_lcmd));  // open: op_addr
  or or_1 (or_1_out, comparator_1_eq, comparator_2_eq, comparator_3_eq);
  Multiplexer #(.Bits(9)) multiplexer_1 (.sel(op_lflag), .in_0(entry64_d), .in_1(entry16_d), .out(multiplexer_1_out));
  not not_1 (not_1_out, uop[45]);
  and and_1 (and_1_out, or_1_out, not_1_out);
  Multiplexer #(.Bits(9)) multiplexer_2 (
    .sel(and_1_out), .in_0(multiplexer_1_out), .in_1(9'h16), .out(multiplexer_2_out));
  Multiplexer #(.Bits(9)) multiplexer_3 (.sel(irq), .in_0(multiplexer_2_out), .in_1(9'h17), .out(multiplexer_3_out));
  Add #(.Bits(9)) add_1 (.a(9'h1), .b(uPC_q), .c_i(1'b0), .s(add_1_s));  // open: c_o
  Multiplexer #(.Bits(9)) multiplexer_4 (
    .sel(decode), .in_0(add_1_s), .in_1(multiplexer_3_out), .out(multiplexer_4_out));
  Multiplexer #(.Bits(9)) multiplexer_5 (
    .sel(branch), .in_0(multiplexer_4_out), .in_1(uop[8:0]), .out(multiplexer_5_out));
  Register #(.Bits(9)) uPC (.D(multiplexer_7_out), .C(clk), .en(1'b1), .Q(uPC_q));
  Multiplexer #(.Bits(9)) multiplexer_6 (.sel(busy), .in_0(multiplexer_5_out), .in_1(uPC_q), .out(multiplexer_6_out));
  Multiplexer #(.Bits(9)) multiplexer_7 (
    .sel(reset), .in_0(multiplexer_6_out), .in_1({9{1'b1}}), .out(multiplexer_7_out));
  ROM #(.AddrBits(9), .Bits(51)) uROM (.A(multiplexer_7_out), .sel(1'b1), .D(uROM_d));
  Multiplexer #(.Bits(51)) multiplexer_8 (.sel(reset), .in_0(uROM_d), .in_1({51{1'b0}}), .out(multiplexer_8_out));
  Register #(.Bits(51)) u_uop (.D(multiplexer_8_out), .C(clk), .en(1'b1), .Q(uop));

  // Other names for the same wires on the sheet: P_IMM[8:0] = uop[8:0]; P_C_ACTIVE = uop[45]
endmodule
